# Fritzing sketch elec_schema (saved by Fritzing 0.7.0b)
breadboards: 1

parts:
  Arduino1 = Arduino
  R1 = Resistor [tolerance=±5% resistance=220 package=THT]
  R2 = Resistor [tolerance=±5% resistance=220 package=THT]
  LED1 = LED - 5mm [color="Infrared (850nm)" package="5 mm [THT]"]
  R3 = Photocell (LDR) [package=THT]
  LED2 = LED - 5mm [color="Red (633nm)" package="5 mm [THT]"]
  R4 = Resistor [tolerance=±5% resistance=220 package=THT]

nets:
  N1: Arduino1.GND, R1.Pin_1, R2.Pin_1, R4.Pin_0
  N2: Arduino1.D9, LED2.cathode
  N3: Arduino1.D8, LED1.cathode
  N4: Arduino1.+5V, R3.pin_0
  N5: Arduino1.A0, R2.Pin_0, R3.pin_1
  N6: R1.Pin_0, LED1.anode
  N7: LED2.anode, R4.Pin_1
